# Fritzing sketch pico_power (saved by Fritzing 1.0.1rc)
breadboards: 1

parts:
  L298N1 = L298N DC motor driver
  Mod1 = Raspberry Pi Pico W
  D1 = Diode [package=diode-hv]
  U1 = LIPO-1000mAh [package=lipo-1000]
  S1 = Toggle Switch spst [package=THT]

nets:
  N1: L298N1.12V, S1.COM
  N2: L298N1.GND, Mod1.pin_3, Mod1.pin_8, Mod1.pin_13, Mod1.pin_18, Mod1.pin_23, Mod1.pin_28, Mod1.pin_33, Mod1.pin_38, U1.-
  N3: L298N1.5V, D1.A
  N4: Mod1.pin_39, D1.C
  N5: U1.+, S1.L1

notes:
  5V
  3V3
  11.1 Volt
  Lithium polymer
  Battery

custom parts:
  L298N DC motor driver: 2x DC motor driver with 78M05 positive voltage regulator (7..35 V) L298N: max 46 V, 2 A Set 5 V Enable jumper to enable 5 V regultor (needed for the L298N) and +5 V output at screw terminal or supply external +5 V at screw terminal Set ENA and/or ENB to +5 V to enable motor permanently or supply ENA and/or ENB with PWM signal IN1 and IN2 set rotation directory for motor A (OUT1/OUT2) IN2 and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
  Raspberry Pi Pico W: Raspberry Pi Pico W. Based around the RP2040 microcontroller the Pico W is a low cost microcontroller device bringing Raspberry Pi quality, cost, and easy of use to the microcontroller space. The areas marked KEEPOUT in pcb silkscreen should not have traces running through them to avoid shorts on a soldered in module!
  Toggle Switch spst: Toggle Switch single pole single throw
